# Fritzing sketch AlarmSystem (saved by Fritzing 0.9.3b)
breadboards: 1

parts:
  PART1 = SparkFun Photon RedBoard [part_number=DEV-13321]
  S1 = Pushbutton [part_number=PRT-14460 package="[THT]"]
  S2 = Pushbutton [part_number=PRT-14460 package="[THT]"]
  S3 = Pushbutton [part_number=PRT-14460 package="[THT]"]
  SG1 = Buzzer 12mm [part_number=COM-07950 package=buzzer-12mm-ns]
  SparkFun_Micro_OLED_Breakout1 = SparkFun Micro OLED Breakout [part_number=LCD-13003]  # not connected
  S4 = Reed switch [package=THT]

nets:
  N1: PART1.D1, S4.pin_1
  N2: PART1.GND#56, S4.pin_2
  N3: PART1.D5, S1.Pin_3, S1.Pin_4
  N4: PART1.D4, S2.Pin_3, S2.Pin_4
  N5: PART1.D3, S3.Pin_3, S3.Pin_4
  N6: PART1.D2, SG1.1
  N7: PART1.GND#117, S1.Pin_1, S1.Pin_2, S2.Pin_1, S2.Pin_2, S3.Pin_1, S3.Pin_2, SG1.2

custom parts:
  SparkFun Photon RedBoard: SparkFun RedBoard for Photon has the P1 module in an Arduino Uno R3 footprint. Please visit: www.sparkfun.com/products/13321
  Pushbutton: A generic pushbutton. This is a simple 4-pack of multicolor buttons, great for all sorts of projects! Unlike previous iterations of multicolor buttons, this pack’s tactile switches are actually recessed into the housing so they don’t accidentally fall off during use. Each pack comes with one red button, one blue button, one yellow button and one green button. These are the same buttons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
  Pushbutton: A generic pushbutton. This is a simple 4-pack of multicolor buttons, great for all sorts of projects! Unlike previous iterations of multicolor buttons, this pack’s tactile switches are actually recessed into the housing so they don’t accidentally fall off during use. Each pack comes with one red button, one blue button, one yellow button and one green button. These are the same buttons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
  Pushbutton: A generic pushbutton. This is a simple 4-pack of multicolor buttons, great for all sorts of projects! Unlike previous iterations of multicolor buttons, this pack’s tactile switches are actually recessed into the housing so they don’t accidentally fall off during use. Each pack comes with one red button, one blue button, one yellow button and one green button. These are the same buttons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
  Buzzer 12mm: Buzzer 12mm Spark Fun Electronics SKU : Comp-Buzzer Through hole This is a small 12mm round speaker that operates around the audible 2kHz range. You can use these speakers to create simple music or user interfaces. This is not a true piezoelectric speaker but behaves similarly. Instead of a piezoelectric crystal that vibrates with an electric current, this tiny speaker uses an electromagnet to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
  SparkFun Micro OLED Breakout: Description: The SparkFun Micro OLED Breakout Board breaks out a small monochrome, blue-on-black OLED. It’s “micro”, but it still packs a punch – the OLED display is crisp, and you can fit a deceivingly large amount of graphics on there. This breakout is perfect for adding graphics to your next Arduino project, displaying diagnostic information without resorting to serial output, and teaching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
